// Logisim project snake.circ as structural Verilog: 7 circuits, main circuit main
module main (
);

  wire and_1_out, Bewegungstakt_out, clock_1_out, d_ff_1_q, eq_1_out_3, eq_2_out_3, eq_3_out_3,
       keycomp_input, or_1_out, or_3_out, reset_out, schlange_1_kollision;
  wire [1:0] keycomp_out_2, register_1_q;
  wire [3:0] apfel_1_out_3, apfel_1_out_4, counter_1_q, player_1_x, player_1_y;
  wire [6:0] keyboard_1_data;
  wire [15:0] decoder_1_out0, or_2_out, register_2_q, register_3_q, register_4_q, register_5_q, register_6_q,
       register_7_q, register_8_q, register_9_q, register_10_q, register_11_q, register_12_q, register_13_q,
       register_14_q, register_15_q, register_16_q, register_17_q, rom_1_data, rom_2_data, schlange_1_out_8;
  wire [16:0] demultiplexer_1_out0, demultiplexer_1_out1, demultiplexer_1_out2, demultiplexer_1_out3,
       demultiplexer_1_out4, demultiplexer_1_out5, demultiplexer_1_out6, demultiplexer_1_out7,
       demultiplexer_1_out8, demultiplexer_1_out9, demultiplexer_1_out10, demultiplexer_1_out11,
       demultiplexer_1_out12, demultiplexer_1_out13, demultiplexer_1_out14, demultiplexer_1_out15;
  wire [16:1] multiplexer_1_out;

  Counter #(.width(4), .max('hf)) counter_1 (.Q(counter_1_q), .clk(clock_1_out));  // open: load, D, count, carry, clr
  Clock clock_1 (.out(clock_1_out));
  ROM #(.addrWidth(4), .dataWidth(16)) rom_1 (.addr(counter_1_q), .data(rom_1_data));  // open: sel
  ROM #(.addrWidth(4), .dataWidth(16)) rom_2 (.addr(counter_1_q), .data(rom_2_data));  // open: sel
  keycomp keycomp (.in_1(keyboard_1_data), .out_2(keycomp_out_2), .\input (keycomp_input));
  Keyboard keyboard_1 (.clk(clock_1_out), .data(keyboard_1_data));  // open: re, clr, avail
  Register #(.width(2)) register_1 (
    .D(keycomp_out_2), .en(keycomp_input), .Q(register_1_q), .clk(clock_1_out));  // open: clr
  Clock #(.highDuration(16), .lowDuration(16)) Bewegungstakt (.out(Bewegungstakt_out));
  player player_1 (.\input (register_1_q), .move(1'b1), .takt(Bewegungstakt_out), .x(player_1_x), .y(player_1_y));
  Button reset (.out(reset_out));
  schlange schlange_1 (
    .x_abfrage(counter_1_q), .p_x(player_1_x), .p_y(player_1_y), .schritt(Bewegungstakt_out),
    .reset(reset_out), .len_plus_plus(and_1_out), .out_8(schlange_1_out_8), .kollision(schlange_1_kollision));
  or or_1 (or_1_out, and_1_out, reset_out);
  apfel apfel_1 (.neu(or_1_out), .in_2(Bewegungstakt_out), .out_3(apfel_1_out_3), .out_4(apfel_1_out_4));
  DotMatrix #(.matrixcols(16), .matrixrows(16)) dotmatrix_1 (
    .col0(register_2_q), .col1(register_3_q), .col2(register_4_q), .col3(register_5_q), .col4(register_6_q),
    .col5(register_7_q), .col6(register_8_q), .col7(register_9_q), .col8(register_10_q),
    .col9(register_11_q), .col10(register_12_q), .col11(register_13_q), .col12(register_14_q),
    .col13(register_15_q), .col14(register_16_q), .col15(register_17_q));
  eq eq_1 (.in_1(player_1_y), .in_2(apfel_1_out_3), .out_3(eq_1_out_3));
  eq eq_2 (.in_1(apfel_1_out_4), .in_2(player_1_x), .out_3(eq_2_out_3));
  and and_1 (and_1_out, eq_1_out_3, eq_2_out_3);
  eq eq_3 (.in_1(apfel_1_out_4), .in_2(counter_1_q), .out_3(eq_3_out_3));
  Decoder #(.select(4), .disabled(0)) decoder_1 (
    .out0(decoder_1_out0[0]), .out1(decoder_1_out0[1]), .out2(decoder_1_out0[2]), .out3(decoder_1_out0[3]),
    .out4(decoder_1_out0[4]), .out5(decoder_1_out0[5]), .out6(decoder_1_out0[6]), .out7(decoder_1_out0[7]),
    .out8(decoder_1_out0[8]), .out9(decoder_1_out0[9]), .out10(decoder_1_out0[10]),
    .out11(decoder_1_out0[11]), .out12(decoder_1_out0[12]), .out13(decoder_1_out0[13]),
    .out14(decoder_1_out0[14]), .out15(decoder_1_out0[15]), .sel(apfel_1_out_3), .en(eq_3_out_3));
  assign or_2_out = rom_2_data | schlange_1_out_8 | decoder_1_out0;  // OR_Gate or_2, 16 bits wide
  D_Flip_Flop d_ff_1 (.clk(clock_1_out), .D(or_3_out), .Q(d_ff_1_q), .reset(reset_out));  // open: Qn, preset, en
  or or_3 (or_3_out, d_ff_1_q, schlange_1_kollision);
  Multiplexer #(.width(16), .enable("false")) multiplexer_1 (
    .in0(or_2_out), .in1(rom_1_data), .out(multiplexer_1_out), .sel(or_3_out));
  Demultiplexer #(.select(4), .width(17), .enable("false")) demultiplexer_1 (
    .out0(demultiplexer_1_out0), .out1(demultiplexer_1_out1), .out2(demultiplexer_1_out2),
    .out3(demultiplexer_1_out3), .out4(demultiplexer_1_out4), .out5(demultiplexer_1_out5),
    .out6(demultiplexer_1_out6), .out7(demultiplexer_1_out7), .out8(demultiplexer_1_out8),
    .out9(demultiplexer_1_out9), .out10(demultiplexer_1_out10), .out11(demultiplexer_1_out11),
    .out12(demultiplexer_1_out12), .out13(demultiplexer_1_out13), .out14(demultiplexer_1_out14),
    .out15(demultiplexer_1_out15), .in({multiplexer_1_out, 1'b1}), .sel(counter_1_q));
  Register #(.width(16)) register_2 (
    .D(demultiplexer_1_out0[16:1]), .en(demultiplexer_1_out0[0]), .Q(register_2_q), .clk(clock_1_out));  // open: clr
  Register #(.width(16)) register_3 (
    .D(demultiplexer_1_out1[16:1]), .en(demultiplexer_1_out1[0]), .Q(register_3_q), .clk(clock_1_out));  // open: clr
  Register #(.width(16)) register_4 (
    .D(demultiplexer_1_out2[16:1]), .en(demultiplexer_1_out2[0]), .Q(register_4_q), .clk(clock_1_out));  // open: clr
  Register #(.width(16)) register_5 (
    .D(demultiplexer_1_out3[16:1]), .en(demultiplexer_1_out3[0]), .Q(register_5_q), .clk(clock_1_out));  // open: clr
  Register #(.width(16)) register_6 (
    .D(demultiplexer_1_out4[16:1]), .en(demultiplexer_1_out4[0]), .Q(register_6_q), .clk(clock_1_out));  // open: clr
  Register #(.width(16)) register_7 (
    .D(demultiplexer_1_out5[16:1]), .en(demultiplexer_1_out5[0]), .Q(register_7_q), .clk(clock_1_out));  // open: clr
  Register #(.width(16)) register_8 (
    .D(demultiplexer_1_out6[16:1]), .en(demultiplexer_1_out6[0]), .Q(register_8_q), .clk(clock_1_out));  // open: clr
  Register #(.width(16)) register_9 (
    .D(demultiplexer_1_out7[16:1]), .en(demultiplexer_1_out7[0]), .Q(register_9_q), .clk(clock_1_out));  // open: clr
  Register #(.width(16)) register_10 (
    .D(demultiplexer_1_out8[16:1]), .en(demultiplexer_1_out8[0]), .Q(register_10_q), .clk(clock_1_out));  // open: clr
  Register #(.width(16)) register_11 (
    .D(demultiplexer_1_out9[16:1]), .en(demultiplexer_1_out9[0]), .Q(register_11_q), .clk(clock_1_out));  // open: clr
  Register #(.width(16)) register_12 (
    .D(demultiplexer_1_out10[16:1]), .en(demultiplexer_1_out10[0]), .Q(register_12_q), .clk(clock_1_out));  // open: clr
  Register #(.width(16)) register_13 (
    .D(demultiplexer_1_out11[16:1]), .en(demultiplexer_1_out11[0]), .Q(register_13_q), .clk(clock_1_out));  // open: clr
  Register #(.width(16)) register_14 (
    .D(demultiplexer_1_out12[16:1]), .en(demultiplexer_1_out12[0]), .Q(register_14_q), .clk(clock_1_out));  // open: clr
  Register #(.width(16)) register_15 (
    .D(demultiplexer_1_out13[16:1]), .en(demultiplexer_1_out13[0]), .Q(register_15_q), .clk(clock_1_out));  // open: clr
  Register #(.width(16)) register_16 (
    .D(demultiplexer_1_out14[16:1]), .en(demultiplexer_1_out14[0]), .Q(register_16_q), .clk(clock_1_out));  // open: clr
  Register #(.width(16)) register_17 (
    .D(demultiplexer_1_out15[16:1]), .en(demultiplexer_1_out15[0]), .Q(register_17_q), .clk(clock_1_out));  // open: clr

  // Notes on the sheet:
  //   x
  //   contents of rom_1 (hex, n*v repeats v):
  //   0 7e00 4800 487e 4800 4000 4000 0 0 1e7e 2802 4802 4802 2802 1e02
  //   512 Hz Frequenz einstellen!
  //   tastatur
  //   mit zeigefingertool auf tastatureingabe klicken, steuerung mit W A S D
  //   player1
  //   falls nicht reagiert
  //   nochmal auf tastaturding links tippen
endmodule

module player (
  input  [1:0] \input ,
  input  move,
  input  takt,
  output [3:0] x,
  output [3:0] y
);

  wire [2:2] not_1_out;
  wire [3:0] adder_1_out, adder_2_out, multiplexer_1_out, multiplexer_2_out, subtractor_1_out,
       subtractor_2_out;

  not not_1 (not_1_out[2], move);
  Adder #(.width(4)) adder_1 (.a(x), .b(4'b0001), .out(adder_1_out));  // open: cin, cout
  Subtractor #(.width(4)) subtractor_1 (.a(x), .b(4'b0001), .out(subtractor_1_out));  // open: bin, bout
  Adder #(.width(4)) adder_2 (.a(y), .b(4'b0001), .out(adder_2_out));  // open: cin, cout
  Subtractor #(.width(4)) subtractor_2 (.a(y), .b(4'b0001), .out(subtractor_2_out));  // open: bin, bout
  Multiplexer #(.select(3), .width(4), .disabled(0), .enable("false")) multiplexer_1 (
    .in0(x), .in1(adder_1_out), .in2(subtractor_1_out), .in3(x), .in4(x), .in5(x), .in6(x), .in7(x),
    .out(multiplexer_1_out), .sel({not_1_out[2], \input }));
  Multiplexer #(.select(3), .width(4), .disabled(0), .enable("false")) multiplexer_2 (
    .in0(subtractor_2_out), .in1(y), .in2(y), .in3(adder_2_out), .in4(y), .in5(y), .in6(y), .in7(y),
    .out(multiplexer_2_out), .sel({not_1_out[2], \input }));
  Register #(.width(4)) u_x (.D(multiplexer_1_out), .Q(x), .clk(takt));  // open: en, clr
  Register #(.width(4)) u_y (.D(multiplexer_2_out), .Q(y), .clk(takt));  // open: en, clr
endmodule

module keycomp (
  input  [6:0] in_1,
  output [1:0] out_2,
  output \input 
);

  wire and_1_out;
  wire [1:0] and_6_out, and_7_out, and_8_out, and_9_out;
  wire [1:1] and_2_out, and_3_out, and_4_out, and_5_out;
  wire [6:0] xnor_1_out, xnor_2_out, xnor_3_out, xnor_4_out, xnor_5_out;

  assign xnor_1_out = ~(in_1 ^ {7{1'b0}});  // XNOR_Gate xnor_1, 7 bits wide
  assign xnor_2_out = ~(in_1 ^ 7'b1110011);  // XNOR_Gate xnor_2, 7 bits wide
  assign xnor_3_out = ~(in_1 ^ 7'b1100100);  // XNOR_Gate xnor_3, 7 bits wide
  assign xnor_4_out = ~(in_1 ^ 7'b1100001);  // XNOR_Gate xnor_4, 7 bits wide
  assign xnor_5_out = ~(in_1 ^ 7'b1110111);  // XNOR_Gate xnor_5, 7 bits wide
  and and_1 (and_1_out, xnor_1_out[0], xnor_1_out[1], xnor_1_out[2], xnor_1_out[3], xnor_1_out[4], xnor_1_out[5], xnor_1_out[6]);
  and and_2 (and_2_out[1], xnor_2_out[0], xnor_2_out[1], xnor_2_out[2], xnor_2_out[3], xnor_2_out[4], xnor_2_out[5], xnor_2_out[6]);
  and and_3 (and_3_out[1], xnor_3_out[0], xnor_3_out[1], xnor_3_out[2], xnor_3_out[3], xnor_3_out[4], xnor_3_out[5], xnor_3_out[6]);
  and and_4 (and_4_out[1], xnor_4_out[0], xnor_4_out[1], xnor_4_out[2], xnor_4_out[3], xnor_4_out[4], xnor_4_out[5], xnor_4_out[6]);
  and and_5 (and_5_out[1], xnor_5_out[0], xnor_5_out[1], xnor_5_out[2], xnor_5_out[3], xnor_5_out[4], xnor_5_out[5], xnor_5_out[6]);
  assign and_6_out = {2{and_2_out[1]}} & 2'b00;  // AND_Gate and_6, 2 bits wide
  assign and_7_out = {2{and_3_out[1]}} & 2'b01;  // AND_Gate and_7, 2 bits wide
  assign and_8_out = {2{and_4_out[1]}} & 2'b10;  // AND_Gate and_8, 2 bits wide
  assign and_9_out = {2{and_5_out[1]}} & 2'b11;  // AND_Gate and_9, 2 bits wide
  assign out_2 = and_6_out | and_7_out | and_8_out | and_9_out;  // OR_Gate or_1, 2 bits wide
  not not_1 (\input , and_1_out);

  // Notes on the sheet:
  //   s = 00
  //   d = 01
  //   a = 10
  //   w = 11
  //   nichts
endmodule

module apfel (
  input  neu,
  input  in_2,
  output [3:0] out_3,
  output [3:0] out_4
);

  Random random_1 (.clk(in_2), .next(neu), .out({out_4, out_3}));  // open: clr
endmodule

module eq (
  input  [3:0] in_1,
  input  [3:0] in_2,
  output out_3
);

  wire [3:0] xnor_1_out;

  assign xnor_1_out = ~(in_1 ^ in_2);  // XNOR_Gate xnor_1, 4 bits wide
  and and_1 (out_3, xnor_1_out[0], xnor_1_out[1], xnor_1_out[2], xnor_1_out[3]);
endmodule

module schlange (
  input  [3:0] x_abfrage,
  input  [3:0] p_x,
  input  [3:0] p_y,
  input  schritt,
  input  reset,
  input  len_plus_plus,
  output kollision,
  output [15:0] out_8
);

  wire button_1_out, eq_1_out_3, or_2_out;
  wire [4:0] counter_1_q, schlangensegment_1_out_6, schlangensegment_2_out_6, schlangensegment_3_out_6,
       schlangensegment_4_out_6, schlangensegment_5_out_6, schlangensegment_6_out_6,
       schlangensegment_7_out_6, schlangensegment_8_out_6, schlangensegment_9_out_6,
       schlangensegment_10_out_6, schlangensegment_11_out_6, schlangensegment_12_out_6,
       schlangensegment_13_out_6, schlangensegment_14_out_6, schlangensegment_15_out_6,
       schlangensegment_16_out_6, schlangensegment_17_out_6, schlangensegment_18_out_6,
       schlangensegment_19_out_6, schlangensegment_20_out_6, schlangensegment_21_out_6,
       schlangensegment_22_out_6, schlangensegment_23_out_6, schlangensegment_24_out_6,
       schlangensegment_25_out_6, schlangensegment_26_out_6, schlangensegment_27_out_6,
       schlangensegment_28_out_6, schlangensegment_30_out_6, schlangensegment_31_out_6,
       schlangensegment_32_out_6;
  wire [7:0] max_len___32_q0, max_len___32_q1, max_len___32_q2, max_len___32_q3, max_len___32_q4,
       max_len___32_q5, max_len___32_q6, max_len___32_q7, max_len___32_q8, max_len___32_q9, max_len___32_q10,
       max_len___32_q11, max_len___32_q12, max_len___32_q13, max_len___32_q14, max_len___32_q15,
       max_len___32_q16, max_len___32_q17, max_len___32_q18, max_len___32_q19, max_len___32_q20,
       max_len___32_q21, max_len___32_q22, max_len___32_q23, max_len___32_q24, max_len___32_q25,
       max_len___32_q26, max_len___32_q27, max_len___32_q28, max_len___32_q29, max_len___32_q30,
       max_len___32_q31;
  wire [16:0] schlangensegment_1_out_5, schlangensegment_2_out_5, schlangensegment_3_out_5,
       schlangensegment_4_out_5, schlangensegment_5_out_5, schlangensegment_6_out_5,
       schlangensegment_7_out_5, schlangensegment_8_out_5, schlangensegment_9_out_5,
       schlangensegment_10_out_5, schlangensegment_11_out_5, schlangensegment_12_out_5,
       schlangensegment_13_out_5, schlangensegment_14_out_5, schlangensegment_16_out_5,
       schlangensegment_17_out_5, schlangensegment_18_out_5, schlangensegment_19_out_5,
       schlangensegment_20_out_5, schlangensegment_21_out_5, schlangensegment_23_out_5,
       schlangensegment_24_out_5, schlangensegment_26_out_5;
  wire [16:1] decoder_1_out0;

  Shift_Register #(.width(8), .length(32)) max_len___32 (
    .in({p_y, p_x}), .clk(schritt), .clr(reset), .q0(max_len___32_q0), .q1(max_len___32_q1),
    .q2(max_len___32_q2), .q3(max_len___32_q3), .q4(max_len___32_q4), .q5(max_len___32_q5),
    .q6(max_len___32_q6), .q7(max_len___32_q7), .q8(max_len___32_q8), .q9(max_len___32_q9),
    .q10(max_len___32_q10), .q11(max_len___32_q11), .q12(max_len___32_q12), .q13(max_len___32_q13),
    .q14(max_len___32_q14), .q15(max_len___32_q15), .q16(max_len___32_q16), .q17(max_len___32_q17),
    .q18(max_len___32_q18), .q19(max_len___32_q19), .q20(max_len___32_q20), .q21(max_len___32_q21),
    .q22(max_len___32_q22), .q23(max_len___32_q23), .q24(max_len___32_q24), .q25(max_len___32_q25),
    .q26(max_len___32_q26), .q27(max_len___32_q27), .q28(max_len___32_q28), .q29(max_len___32_q29),
    .q30(max_len___32_q30), .q31(max_len___32_q31));  // open: shift, out, load, d0, d1, d2, d3, d4, d5, d6, d7, d8, d9, d10, d11, d12, d13, d14, d15, d16, d17, d18, d19, d20, d21, d22, d23, d24, d25, d26, d27, d28, d29, d30, d31
  schlangensegment schlangensegment_1 (
    .\input (max_len___32_q2), .x_abfrage(x_abfrage), .out_5(schlangensegment_1_out_5),
    .in_4(schlangensegment_3_out_6), .out_6(schlangensegment_1_out_6), .p_pos({p_y, p_x}));
  schlangensegment schlangensegment_2 (
    .\input (max_len___32_q0), .x_abfrage(x_abfrage), .out_5(schlangensegment_2_out_5), .in_4(counter_1_q),
    .out_6(schlangensegment_2_out_6), .p_pos({p_y, p_x}));
  schlangensegment schlangensegment_3 (
    .\input (max_len___32_q1), .x_abfrage(x_abfrage), .out_5(schlangensegment_3_out_5),
    .in_4(schlangensegment_2_out_6), .out_6(schlangensegment_3_out_6), .p_pos({p_y, p_x}));
  schlangensegment schlangensegment_4 (
    .\input (max_len___32_q5), .x_abfrage(x_abfrage), .out_5(schlangensegment_4_out_5),
    .in_4(schlangensegment_11_out_6), .out_6(schlangensegment_4_out_6), .p_pos({p_y, p_x}));
  schlangensegment schlangensegment_5 (
    .\input (max_len___32_q8), .x_abfrage(x_abfrage), .out_5(schlangensegment_5_out_5),
    .in_4(schlangensegment_9_out_6), .out_6(schlangensegment_5_out_6), .p_pos({p_y, p_x}));
  schlangensegment schlangensegment_6 (
    .\input (max_len___32_q6), .x_abfrage(x_abfrage), .out_5(schlangensegment_6_out_5),
    .in_4(schlangensegment_4_out_6), .out_6(schlangensegment_6_out_6), .p_pos({p_y, p_x}));
  schlangensegment schlangensegment_7 (
    .\input (max_len___32_q9), .x_abfrage(x_abfrage), .out_5(schlangensegment_7_out_5),
    .in_4(schlangensegment_5_out_6), .out_6(schlangensegment_7_out_6), .p_pos({p_y, p_x}));
  schlangensegment schlangensegment_8 (
    .\input (max_len___32_q10), .x_abfrage(x_abfrage), .out_5(schlangensegment_8_out_5),
    .in_4(schlangensegment_7_out_6), .out_6(schlangensegment_8_out_6), .p_pos({p_y, p_x}));
  schlangensegment schlangensegment_9 (
    .\input (max_len___32_q7), .x_abfrage(x_abfrage), .out_5(schlangensegment_9_out_5),
    .in_4(schlangensegment_6_out_6), .out_6(schlangensegment_9_out_6), .p_pos({p_y, p_x}));
  schlangensegment schlangensegment_10 (
    .\input (max_len___32_q3), .x_abfrage(x_abfrage), .out_5(schlangensegment_10_out_5),
    .in_4(schlangensegment_1_out_6), .out_6(schlangensegment_10_out_6), .p_pos({p_y, p_x}));
  schlangensegment schlangensegment_11 (
    .\input (max_len___32_q4), .x_abfrage(x_abfrage), .out_5(schlangensegment_11_out_5),
    .in_4(schlangensegment_10_out_6), .out_6(schlangensegment_11_out_6), .p_pos({p_y, p_x}));
  eq eq_1 (.in_1(x_abfrage), .in_2(p_x), .out_3(eq_1_out_3));
  Counter #(.width(5), .max('h1e), .ongoal("stay")) counter_1 (
    .count(or_2_out), .Q(counter_1_q), .clk(schritt), .clr(reset));  // open: load, D, carry
  schlangensegment schlangensegment_12 (
    .\input (max_len___32_q14), .x_abfrage(x_abfrage), .out_5(schlangensegment_12_out_5),
    .in_4(schlangensegment_16_out_6), .out_6(schlangensegment_12_out_6), .p_pos({p_y, p_x}));
  schlangensegment schlangensegment_13 (
    .\input (max_len___32_q17), .x_abfrage(x_abfrage), .out_5(schlangensegment_13_out_5),
    .in_4(schlangensegment_15_out_6), .out_6(schlangensegment_13_out_6), .p_pos({p_y, p_x}));
  schlangensegment schlangensegment_14 (
    .\input (max_len___32_q15), .x_abfrage(x_abfrage), .out_5(schlangensegment_14_out_5),
    .in_4(schlangensegment_12_out_6), .out_6(schlangensegment_14_out_6), .p_pos({p_y, p_x}));
  schlangensegment schlangensegment_15 (
    .\input (max_len___32_q16), .x_abfrage(x_abfrage), .in_4(schlangensegment_14_out_6),
    .out_6(schlangensegment_15_out_6), .p_pos({p_y, p_x}));  // open: out_5
  schlangensegment schlangensegment_16 (
    .\input (max_len___32_q13), .x_abfrage(x_abfrage), .out_5(schlangensegment_16_out_5),
    .in_4(schlangensegment_18_out_6), .out_6(schlangensegment_16_out_6), .p_pos({p_y, p_x}));
  schlangensegment schlangensegment_17 (
    .\input (max_len___32_q11), .x_abfrage(x_abfrage), .out_5(schlangensegment_17_out_5),
    .in_4(schlangensegment_8_out_6), .out_6(schlangensegment_17_out_6), .p_pos({p_y, p_x}));
  schlangensegment schlangensegment_18 (
    .\input (max_len___32_q12), .x_abfrage(x_abfrage), .out_5(schlangensegment_18_out_5),
    .in_4(schlangensegment_17_out_6), .out_6(schlangensegment_18_out_6), .p_pos({p_y, p_x}));
  schlangensegment schlangensegment_19 (
    .\input (max_len___32_q18), .x_abfrage(x_abfrage), .out_5(schlangensegment_19_out_5),
    .in_4(schlangensegment_13_out_6), .out_6(schlangensegment_19_out_6), .p_pos({p_y, p_x}));
  assign {out_8, kollision} = schlangensegment_2_out_5 | schlangensegment_3_out_5 | schlangensegment_1_out_5 | schlangensegment_10_out_5 | schlangensegment_11_out_5 | schlangensegment_4_out_5 | schlangensegment_6_out_5 | schlangensegment_9_out_5 | schlangensegment_5_out_5 | schlangensegment_7_out_5 | schlangensegment_8_out_5 | schlangensegment_17_out_5 | schlangensegment_18_out_5 | schlangensegment_16_out_5 | schlangensegment_12_out_5 | schlangensegment_14_out_5 | schlangensegment_13_out_5 | schlangensegment_19_out_5 | schlangensegment_23_out_5 | schlangensegment_26_out_5 | schlangensegment_20_out_5 | schlangensegment_21_out_5 | schlangensegment_24_out_5 | {decoder_1_out0, 1'b0};  // OR_Gate or_1, 17 bits wide
  Decoder #(.select(4), .disabled(0)) decoder_1 (
    .out0(decoder_1_out0[1]), .out1(decoder_1_out0[2]), .out2(decoder_1_out0[3]), .out3(decoder_1_out0[4]),
    .out4(decoder_1_out0[5]), .out5(decoder_1_out0[6]), .out6(decoder_1_out0[7]), .out7(decoder_1_out0[8]),
    .out8(decoder_1_out0[9]), .out9(decoder_1_out0[10]), .out10(decoder_1_out0[11]),
    .out11(decoder_1_out0[12]), .out12(decoder_1_out0[13]), .out13(decoder_1_out0[14]),
    .out14(decoder_1_out0[15]), .out15(decoder_1_out0[16]), .sel(p_y), .en(eq_1_out_3));
  or or_2 (or_2_out, len_plus_plus, button_1_out);
  schlangensegment schlangensegment_20 (
    .\input (max_len___32_q21), .x_abfrage(x_abfrage), .out_5(schlangensegment_20_out_5),
    .in_4(schlangensegment_26_out_6), .out_6(schlangensegment_20_out_6), .p_pos({p_y, p_x}));
  schlangensegment schlangensegment_21 (
    .\input (max_len___32_q22), .x_abfrage(x_abfrage), .out_5(schlangensegment_21_out_5),
    .in_4(schlangensegment_20_out_6), .out_6(schlangensegment_21_out_6), .p_pos({p_y, p_x}));
  schlangensegment schlangensegment_22 (
    .\input (max_len___32_q26), .x_abfrage(x_abfrage), .in_4(schlangensegment_25_out_6),
    .out_6(schlangensegment_22_out_6), .p_pos({p_y, p_x}));  // open: out_5
  schlangensegment schlangensegment_23 (
    .\input (max_len___32_q19), .x_abfrage(x_abfrage), .out_5(schlangensegment_23_out_5),
    .in_4(schlangensegment_19_out_6), .out_6(schlangensegment_23_out_6), .p_pos({p_y, p_x}));
  schlangensegment schlangensegment_24 (
    .\input (max_len___32_q23), .x_abfrage(x_abfrage), .out_5(schlangensegment_24_out_5),
    .in_4(schlangensegment_21_out_6), .out_6(schlangensegment_24_out_6), .p_pos({p_y, p_x}));
  schlangensegment schlangensegment_25 (
    .\input (max_len___32_q25), .x_abfrage(x_abfrage), .in_4(schlangensegment_27_out_6),
    .out_6(schlangensegment_25_out_6), .p_pos({p_y, p_x}));  // open: out_5
  schlangensegment schlangensegment_26 (
    .\input (max_len___32_q20), .x_abfrage(x_abfrage), .out_5(schlangensegment_26_out_5),
    .in_4(schlangensegment_23_out_6), .out_6(schlangensegment_26_out_6), .p_pos({p_y, p_x}));
  schlangensegment schlangensegment_27 (
    .\input (max_len___32_q24), .x_abfrage(x_abfrage), .in_4(schlangensegment_24_out_6),
    .out_6(schlangensegment_27_out_6), .p_pos({p_y, p_x}));  // open: out_5
  Button button_1 (.out(button_1_out));
  schlangensegment schlangensegment_28 (
    .\input (max_len___32_q27), .x_abfrage(x_abfrage), .in_4(schlangensegment_22_out_6),
    .out_6(schlangensegment_28_out_6), .p_pos({p_y, p_x}));  // open: out_5
  schlangensegment schlangensegment_29 (
    .\input (max_len___32_q31), .x_abfrage(x_abfrage), .in_4(schlangensegment_32_out_6), .p_pos({p_y, p_x}));  // open: out_5, out_6
  schlangensegment schlangensegment_30 (
    .\input (max_len___32_q29), .x_abfrage(x_abfrage), .in_4(schlangensegment_31_out_6),
    .out_6(schlangensegment_30_out_6), .p_pos({p_y, p_x}));  // open: out_5
  schlangensegment schlangensegment_31 (
    .\input (max_len___32_q28), .x_abfrage(x_abfrage), .in_4(schlangensegment_28_out_6),
    .out_6(schlangensegment_31_out_6), .p_pos({p_y, p_x}));  // open: out_5
  schlangensegment schlangensegment_32 (
    .\input (max_len___32_q30), .x_abfrage(x_abfrage), .in_4(schlangensegment_30_out_6),
    .out_6(schlangensegment_32_out_6), .p_pos({p_y, p_x}));  // open: out_5

  // Notes on the sheet:
  //   kopf
  //   <-- schlangensegmente
endmodule

module schlangensegment (
  input  [7:0] p_pos,
  input  [7:0] \input ,
  input  [3:0] x_abfrage,
  input  [4:0] in_4,
  output [16:0] out_5,
  output [4:0] out_6
);

  wire and_2_out, eq_1_out_3, eq_2_out_3, eq_3_out_3, not_1_out, subtractor_1_bout;
  wire [4:0] subtractor_1_out;

  Subtractor #(.width(5)) subtractor_1 (
    .a(in_4), .b(5'b00001), .out(subtractor_1_out), .bout(subtractor_1_bout));  // open: bin
  not not_1 (not_1_out, subtractor_1_bout);
  eq eq_1 (.in_1(p_pos[3:0]), .in_2(\input [3:0]), .out_3(eq_1_out_3));
  eq eq_2 (.in_1(p_pos[7:4]), .in_2(\input [7:4]), .out_3(eq_2_out_3));
  eq eq_3 (.in_1(\input [3:0]), .in_2(x_abfrage), .out_3(eq_3_out_3));
  and and_1 (out_5[0], eq_1_out_3, eq_2_out_3, not_1_out);
  and and_2 (and_2_out, eq_3_out_3, not_1_out);
  Multiplexer #(.width(5), .enable("false")) multiplexer_1 (
    .in0({5{1'b0}}), .in1(subtractor_1_out), .out(out_6), .sel(not_1_out));
  Decoder #(.select(4), .disabled(0)) decoder_1 (
    .out0(out_5[1]), .out1(out_5[2]), .out2(out_5[3]), .out3(out_5[4]), .out4(out_5[5]), .out5(out_5[6]),
    .out6(out_5[7]), .out7(out_5[8]), .out8(out_5[9]), .out9(out_5[10]), .out10(out_5[11]),
    .out11(out_5[12]), .out12(out_5[13]), .out13(out_5[14]), .out14(out_5[15]), .out15(out_5[16]),
    .sel(\input [7:4]), .en(and_2_out));
endmodule
